// Logisim project main file.circ as structural Verilog
module _1_bit_ALU (
  input  Cin,
  input  A,
  input  A_Invert,
  input  B,
  input  B_Invert,
  input  [1:0] Select_Bit_Operation,
  output Result,
  output Cout
);

  wire adder_1_out, AND_out, multiplexer_1_out, multiplexer_2_out, not_1_out, not_2_out, OR_out, xor_out;

  not not_1 (not_1_out, A);
  not not_2 (not_2_out, B);
  Multiplexer multiplexer_1 (.in0(A), .in1(not_1_out), .out(multiplexer_1_out), .sel(A_Invert));  // open: en
  Multiplexer multiplexer_2 (.in0(B), .in1(not_2_out), .out(multiplexer_2_out), .sel(B_Invert));  // open: en
  and AND (AND_out, multiplexer_1_out, multiplexer_2_out);
  or OR (OR_out, multiplexer_1_out, multiplexer_2_out);
  xor \xor  (xor_out, multiplexer_1_out, multiplexer_2_out);
  Adder #(.width(1)) adder_1 (.a(multiplexer_1_out), .b(multiplexer_2_out), .out(adder_1_out), .cin(Cin), .cout(Cout));
  Multiplexer #(.select(2)) multiplexer_3 (
    .in0(AND_out), .in1(OR_out), .in2(xor_out), .in3(adder_1_out), .out(Result), .sel(Select_Bit_Operation));  // open: en

  // Notes on the sheet:
  //   Figure: 1-bit Arithmetic Logic Unit.
  //   0
  //   0
  //   0
  //   1
  //   OP2 OP1 OP0  Operation
  //   0
  //   0
  //   1
  //   0
  //   1
  //   0
  //   1
  //   0
  //   AND
  //   OR
  //   ADD
  //   SUB
endmodule

module Register_File (
  input  Clock,
  input  [9:0] Write_Data_IN,
  input  RegWrite,
  input  [1:0] RS,
  input  [1:0] RD,
  input  [1:0] RT,
  output [9:0] Data01,
  output [9:0] Data02
);

  wire and_1_out, and_2_out, and_3_out, and_4_out, decoder_1_out0, decoder_1_out1, decoder_1_out2,
       decoder_1_out3;
  wire [9:0] register_1_q, register_2_q, register_3_q, register_4_q;

  Decoder #(.select(2)) decoder_1 (
    .out0(decoder_1_out0), .out1(decoder_1_out1), .out2(decoder_1_out2), .out3(decoder_1_out3), .sel(RD));  // open: en
  and and_1 (and_1_out, RegWrite, decoder_1_out0);
  and and_2 (and_2_out, RegWrite, decoder_1_out1);
  and and_3 (and_3_out, RegWrite, decoder_1_out2);
  and and_4 (and_4_out, RegWrite, decoder_1_out3);
  Register #(.width(10)) register_1 (.D(Write_Data_IN), .en(and_1_out), .Q(register_1_q), .clk(Clock));  // open: clr
  Register #(.width(10)) register_2 (.D(Write_Data_IN), .en(and_2_out), .Q(register_2_q), .clk(Clock));  // open: clr
  Register #(.width(10)) register_3 (.D(Write_Data_IN), .en(and_3_out), .Q(register_3_q), .clk(Clock));  // open: clr
  Register #(.width(10)) register_4 (.D(Write_Data_IN), .en(and_4_out), .Q(register_4_q), .clk(Clock));  // open: clr
  Multiplexer #(.select(2), .width(10)) multiplexer_1 (
    .in0(register_1_q), .in1(register_2_q), .in2(register_3_q), .in3(register_4_q), .out(Data01), .sel(RS));  // open: en
  Multiplexer #(.select(2), .width(10)) multiplexer_2 (
    .in0(register_1_q), .in1(register_2_q), .in2(register_3_q), .in3(register_4_q), .out(Data02), .sel(RT));  // open: en
endmodule

module R_Type (
  input  in_1,
  input  in_2,
  input  Cin,
  input  Reset,
  input  CLK,
  input  RegWrite,
  output out_7,
  output [9:0] Data
);

  wire [1:0] adder_1_out, bit_extender_1_out, bit_extender_2_out, register_1_q;
  wire [9:0] register_file_1_data01, register_file_1_data02, rom_1_data;

  Register #(.width(2)) register_1 (.D(adder_1_out), .Q(register_1_q), .clk(CLK), .clr(Reset));  // open: en
  Adder #(.width(2)) adder_1 (.a(2'b01), .b(register_1_q), .out(adder_1_out));  // open: cin, cout
  ROM #(.addrWidth(2), .dataWidth(10)) rom_1 (.addr(register_1_q), .data(rom_1_data));  // open: sel
  Bit_Extender #(.in_width(3), .out_width(2)) bit_extender_1 (.out(bit_extender_1_out));  // open: in
  Bit_Extender #(.in_width(3), .out_width(2)) bit_extender_2 (.in(rom_1_data[2:0]), .out(bit_extender_2_out));
  Register_File register_file_1 (
    .Clock(CLK), .Write_Data_IN(Data), .RegWrite(RegWrite), .Data01(register_file_1_data01),
    .RS(rom_1_data[7:6]), .RD(bit_extender_1_out), .Data02(register_file_1_data02), .RT(bit_extender_2_out));
  _10_bit_ALU u_10_bit_alu_1 (
    .Cin(Cin), .Select_Bit(rom_1_data[9:8]), .A_invert(in_1), .B_invert(in_2), .A(register_file_1_data01),
    .out_7(Data), .B(register_file_1_data02), .out_9(out_7));  // open: out_8

  // Notes on the sheet:
  //   contents of rom_1 (hex, n*v repeats v):
  //   2f6 297
  //   Figure: R-Type 10-bit ISA
  //   Instruction Sets
  //   op rd rs rt
  //   add $t6, $s2, $s1
  //   0010 1010 1111 0110
  //   op rs rt rd
  //   0010 1010 1001 0111
  //   op rs rt rd
  //   add $t6, $s2, $s7
  //   2af6
  //   2a97
endmodule

module _10_bit_ALU (
  input  Cin,
  input  [1:0] Select_Bit,
  input  A_invert,
  input  B_invert,
  input  [9:0] A,
  input  [9:0] B,
  output [9:0] out_7,
  output out_8,
  output out_9
);

  wire n1_bit_alu_1_cout, n1_bit_alu_3_cout, n1_bit_alu_4_cout, n1_bit_alu_5_cout, n1_bit_alu_6_cout,
       n1_bit_alu_7_cout, n1_bit_alu_8_cout, n1_bit_alu_9_cout, n1_bit_alu_10_cout;

  _1_bit_ALU u_1_bit_alu_1 (
    .A(A[0]), .A_Invert(A_invert), .Result(out_7[0]), .B(B[0]), .Cout(n1_bit_alu_1_cout),
    .B_Invert(B_invert), .Select_Bit_Operation(Select_Bit), .Cin(Cin));
  _1_bit_ALU u_1_bit_alu_2 (
    .A(A[1]), .A_Invert(A_invert), .Result(out_7[1]), .B(B[1]), .B_Invert(B_invert),
    .Select_Bit_Operation(Select_Bit), .Cin(n1_bit_alu_1_cout));  // open: Cout
  _1_bit_ALU u_1_bit_alu_3 (
    .A(A[2]), .A_Invert(A_invert), .Result(out_7[2]), .B(B[2]), .Cout(n1_bit_alu_3_cout),
    .B_Invert(B_invert), .Select_Bit_Operation(Select_Bit));  // open: Cin
  _1_bit_ALU u_1_bit_alu_4 (
    .A(A[3]), .A_Invert(A_invert), .Result(out_7[3]), .B(B[3]), .Cout(n1_bit_alu_4_cout),
    .B_Invert(B_invert), .Select_Bit_Operation(Select_Bit), .Cin(n1_bit_alu_3_cout));
  _1_bit_ALU u_1_bit_alu_5 (
    .A(A[4]), .A_Invert(A_invert), .Result(out_7[4]), .B(B[4]), .Cout(n1_bit_alu_5_cout),
    .B_Invert(B_invert), .Select_Bit_Operation(Select_Bit), .Cin(n1_bit_alu_4_cout));
  _1_bit_ALU u_1_bit_alu_6 (
    .A(A[5]), .A_Invert(A_invert), .Result(out_7[5]), .B(B[5]), .Cout(n1_bit_alu_6_cout),
    .B_Invert(B_invert), .Select_Bit_Operation(Select_Bit), .Cin(n1_bit_alu_5_cout));
  _1_bit_ALU u_1_bit_alu_7 (
    .A(A[6]), .A_Invert(A_invert), .Result(out_7[6]), .B(B[6]), .Cout(n1_bit_alu_7_cout),
    .B_Invert(B_invert), .Select_Bit_Operation(Select_Bit), .Cin(n1_bit_alu_6_cout));
  _1_bit_ALU u_1_bit_alu_8 (
    .A(A[7]), .A_Invert(A_invert), .Result(out_7[7]), .B(B[7]), .Cout(n1_bit_alu_8_cout),
    .B_Invert(B_invert), .Select_Bit_Operation(Select_Bit), .Cin(n1_bit_alu_7_cout));
  _1_bit_ALU u_1_bit_alu_9 (
    .A(A[8]), .A_Invert(A_invert), .Result(out_7[8]), .B(B[8]), .Cout(n1_bit_alu_9_cout),
    .B_Invert(B_invert), .Select_Bit_Operation(Select_Bit), .Cin(n1_bit_alu_8_cout));
  _1_bit_ALU u_1_bit_alu_10 (
    .A(A[9]), .A_Invert(A_invert), .Result(out_7[9]), .B(B[9]), .Cout(n1_bit_alu_10_cout),
    .B_Invert(B_invert), .Select_Bit_Operation(Select_Bit), .Cin(n1_bit_alu_9_cout));
  xor xor_1 (out_9, n1_bit_alu_9_cout, n1_bit_alu_10_cout);
  nor nor_1 (out_8, out_7[0], out_7[1], out_7[2], out_7[3], out_7[4], out_7[5], out_7[6], out_7[7], out_7[8], out_7[9]);
endmodule

module I_Type (
  input  in_1,
  input  in_2,
  input  Cin,
  input  in_4,
  input  MemWrite,
  input  RegWrite,
  input  MemRead,
  input  in_8,
  input  Reset,
  input  Clock_Pulse,
  output [9:0] out_11,
  output out_12
);

  wire register_file_1_p8;
  wire [1:0] adder_1_out, bit_extender_1_out, bit_extender_3_out, register_1_q;
  wire [9:0] bit_extender_2_out, n10_bit_alu_1_out_7, register_file_1_p4, register_file_1_p7, rom_1_data;

  Register #(.width(2)) register_1 (.D(adder_1_out), .Q(register_1_q), .clk(Clock_Pulse), .clr(Reset));  // open: en
  Adder #(.width(2)) adder_1 (.a(2'b01), .b(register_1_q), .out(adder_1_out));  // open: cin, cout
  ROM #(.addrWidth(2), .dataWidth(10)) rom_1 (.addr(register_1_q), .data(rom_1_data));  // open: sel
  Bit_Extender #(.in_width(3), .out_width(2)) bit_extender_1 (.in(rom_1_data[5:3]), .out(bit_extender_1_out));
  assign bit_extender_2_out = {{7{1'b0}}, rom_1_data[2:0]};  // Bit_Extender bit_extender_2
  // Register_File register_file_1: pin names not known; wires that end beside it: rom_1_data[7:6], bit_extender_1_out, bit_extender_1_out, register_file_1_p4, RegWrite, Clock_Pulse, register_file_1_p7, register_file_1_p8
  _10_bit_ALU u_10_bit_alu_1 (
    .Cin(Cin), .Select_Bit(rom_1_data[9:8]), .A_invert(in_1), .B_invert(in_2), .A(register_file_1_p7),
    .out_7(n10_bit_alu_1_out_7), .B(bit_extender_2_out), .out_8(out_12));  // open: out_9
  Bit_Extender #(.in_width(10), .out_width(2)) bit_extender_3 (.in(n10_bit_alu_1_out_7), .out(bit_extender_3_out));
  RAM #(.addrWidth(2), .dataWidth(10)) ram_1 (
    .addr(bit_extender_3_out), .data(register_file_1_p4), .clk(Clock_Pulse), .ld(MemRead), .clr(in_8));  // open: sel
  Multiplexer #(.width(10)) multiplexer_1 (
    .in0(register_file_1_p4), .in1(register_file_1_p4), .out(out_11), .sel(in_4));  // open: en

  // Notes on the sheet:
  //   contents of rom_1 (hex, n*v repeats v):
  //   2f6 297
  //   Figure: I-Type 16-bit ISA
  //   Instruction Sets
  //   lw $t6, 1($s7)
  //   0010 1010 1111 0001
  //   op rs rd im
  //   sw $t6, 1($s1)
  //   0010 1010 1001 0001
  //   op rs rt im
  //   2af1
  //   2a91
endmodule

module _10_bit_RISC_Processor_with_Pipeline (
  input  in_1,
  input  in_2,
  input  in_3,
  input  in_4,
  input  Reset,
  output out_6,
  output [1:0] RS,
  output [1:0] out_8,
  output [9:0] out_9,
  output out_10,
  output [9:0] out_11,
  output Cout,
  output [9:0] out_13,
  output RW,
  output [9:0] out_15,
  output MW,
  output MR,
  output [1:0] out_18
);

  wire Clock_Pulse_out, control_unit_1_cin, control_unit_1_memread, control_unit_1_memwrite,
       id_ex_pipeline_1_output_2, id_ex_pipeline_1_output_3;
  wire [1:0] bit_extender_4_out;
  wire [2:0] alu_control_1_aluop, bit_extender_2_out;
  wire [3:0] adder_1_out, bit_extender_3_out, control_unit_1_aluop, ex_mem_pipeline_1_address_bit,
       id_ex_pipeline_1_opcode_2, PC_q;
  wire [9:0] bit_extender_1_out, ex_mem_pipeline_1_write_data, id_ex_pipeline_1_data_1,
       id_ex_pipeline_1_data_2, id_ex_pipeline_1_write_data, n10_bit_alu_1_out_7, ram_1_data,
       register_file_1_data01, register_file_1_data02;

  Register #(.width(4)) PC (.D(adder_1_out), .Q(PC_q), .clk(Clock_Pulse_out), .clr(Reset));  // open: en
  Clock Clock_Pulse (.out(Clock_Pulse_out));
  Adder #(.width(4)) adder_1 (.a(4'b0001), .b(PC_q), .out(adder_1_out));  // open: cin, cout
  ROM #(.addrWidth(4), .dataWidth(10)) rom_1 (.addr(PC_q), .data(out_11));  // open: sel
  IF_ID_Pipeline if_id_pipeline_1 (
    .Instruction(out_11), .Clock_Pulse(Clock_Pulse_out), .Data({out_9[9:2], out_8}), .Reset(Reset));
  Control_Unit control_unit_1 (
    .Instruction_Input(out_9[9:6]), .Cin(control_unit_1_cin), .RegWrite(RW),
    .MemWrite(control_unit_1_memwrite), .MemRead(control_unit_1_memread), .ALUOp(control_unit_1_aluop));
  assign bit_extender_1_out = {{8{1'b0}}, out_9[5:4]};  // Bit_Extender bit_extender_1
  Register_File register_file_1 (
    .Clock(Clock_Pulse_out), .Write_Data_IN(id_ex_pipeline_1_write_data), .RegWrite(RW),
    .Data01(register_file_1_data01), .RS(out_8), .RD(out_9[3:2]), .Data02(register_file_1_data02),
    .RT(out_9[3:2]));
  ID_EX_Pipeline id_ex_pipeline_1 (
    .Read_Data_1(register_file_1_data01), .Read_Data_2(register_file_1_data02),
    .Opcode(control_unit_1_aluop), .Immidiate_Value(bit_extender_1_out), .Reset(Reset),
    .Data_1(id_ex_pipeline_1_data_1), .MemWrite_Value(out_15), .Opcode_2(id_ex_pipeline_1_opcode_2),
    .Data_2(id_ex_pipeline_1_data_2), .Result(ex_mem_pipeline_1_write_data),
    .Write_Data(id_ex_pipeline_1_write_data), .MemWrite_2(control_unit_1_memwrite),
    .Output_2(id_ex_pipeline_1_output_2), .MemRead(control_unit_1_memread),
    .Output_3(id_ex_pipeline_1_output_3), .MemWrite(control_unit_1_cin), .Output(out_10),
    .in_9(Clock_Pulse_out));
  Bit_Extender #(.in_width(4), .out_width(3)) bit_extender_2 (.in(id_ex_pipeline_1_opcode_2), .out(bit_extender_2_out));
  _10_bit_ALU u_10_bit_alu_1 (
    .Cin(out_10), .Select_Bit(bit_extender_4_out), .A_invert(in_1), .B_invert(in_2),
    .A(id_ex_pipeline_1_data_1), .out_7(n10_bit_alu_1_out_7), .B(id_ex_pipeline_1_data_2), .out_8(out_6),
    .out_9(Cout));
  ALU_Control alu_control_1 (.F(bit_extender_2_out), .ALUOp(alu_control_1_aluop));
  Bit_Extender #(.in_width(10), .out_width(4)) bit_extender_3 (.in(n10_bit_alu_1_out_7), .out(bit_extender_3_out));
  Bit_Extender #(.in_width(3), .out_width(2)) bit_extender_4 (.in(alu_control_1_aluop), .out(bit_extender_4_out));
  EX_MEM_Pipeline ex_mem_pipeline_1 (
    .Result(bit_extender_3_out), .Read_Data_2(out_15), .Result_2(ram_1_data), .Clock_Pulse(Clock_Pulse_out),
    .Reset(Reset), .Address_Bit(ex_mem_pipeline_1_address_bit), .MemWrite_Value(out_13),
    .Write_Data(ex_mem_pipeline_1_write_data), .MemWrite(id_ex_pipeline_1_output_2), .Output(MW),
    .MemRead(id_ex_pipeline_1_output_3), .Output_2(MR));
  RAM #(.addrWidth(4), .dataWidth(10), .bus("separate")) ram_1 (
    .addr(ex_mem_pipeline_1_address_bit), .din(out_13), .data(ram_1_data), .str(MW), .sel(in_3),
    .clk(Clock_Pulse_out), .ld(MR), .clr(in_4));

  assign out_9[1:0] = out_8;
  assign out_18 = out_9[5:4];
  assign RS = out_9[3:2];

  // Notes on the sheet:
  //   lw $s1, 1($t7)
  //   sw $t0, 3($t5)
  //   OP
  //   OP
  //   2791
  //   0010 0111 1001 0001 
  //   RS
  //   RD
  //   3053
  //   0111 0000 0101 0011 
  //   RT
  //   RS
  //   Im
  //   Im
  //   contents of rom_1 (hex, n*v repeats v):
  //   12 7*0 1
  //   10-Bit RISC Processor with 4 Steps Pipelining (IF-ID-EX-MEM)
endmodule

module IF_ID_Pipeline (
  input  [9:0] Instruction,
  input  Clock_Pulse,
  input  Reset,
  output [9:0] Data
);

  Register #(.width(10)) register_1 (.D(Instruction), .Q(Data), .clk(Clock_Pulse), .clr(Reset));  // open: en
endmodule

module ID_EX_Pipeline (
  input  MemWrite,
  input  [9:0] Read_Data_1,
  input  [9:0] Read_Data_2,
  input  [3:0] Opcode,
  input  [9:0] Immidiate_Value,
  input  [9:0] Result,
  input  MemWrite_2,
  input  MemRead,
  input  in_9,
  input  Reset,
  output Output,
  output [9:0] Data_1,
  output [9:0] MemWrite_Value,
  output [3:0] Opcode_2,
  output [9:0] Data_2,
  output [9:0] Write_Data,
  output Output_2,
  output Output_3
);

  Register #(.width(1)) register_1 (.D(MemWrite), .Q(Output), .clk(in_9), .clr(Reset));  // open: en
  Register #(.width(10)) register_2 (.D(Read_Data_1), .Q(Data_1), .clk(in_9), .clr(Reset));  // open: en
  Register #(.width(10)) register_3 (.D(Read_Data_2), .Q(MemWrite_Value), .clk(in_9), .clr(Reset));  // open: en
  Register #(.width(4)) register_4 (.D(Opcode), .Q(Opcode_2), .clk(in_9), .clr(Reset));  // open: en
  Register #(.width(10)) register_5 (.D(Immidiate_Value), .Q(Data_2), .clk(in_9), .clr(Reset));  // open: en
  Register #(.width(10)) register_6 (.D(Result), .Q(Write_Data), .clk(in_9), .clr(Reset));  // open: en
  Register #(.width(1)) register_7 (.D(MemWrite_2), .Q(Output_2), .clk(in_9), .clr(Reset));  // open: en
  Register #(.width(1)) register_8 (.D(MemRead), .Q(Output_3), .clk(in_9), .clr(Reset));  // open: en
endmodule

module EX_MEM_Pipeline (
  input  [3:0] Result,
  input  [9:0] Read_Data_2,
  input  [9:0] Result_2,
  input  MemWrite,
  input  MemRead,
  input  Clock_Pulse,
  input  Reset,
  output [3:0] Address_Bit,
  output [9:0] MemWrite_Value,
  output [9:0] Write_Data,
  output Output,
  output Output_2
);

  Register #(.width(4)) register_1 (.D(Result), .Q(Address_Bit), .clk(Clock_Pulse), .clr(Reset));  // open: en
  Register #(.width(10)) register_2 (.D(Read_Data_2), .Q(MemWrite_Value), .clk(Clock_Pulse), .clr(Reset));  // open: en
  Register #(.width(10)) register_3 (.D(Result_2), .Q(Write_Data), .clk(Clock_Pulse), .clr(Reset));  // open: en
  Register #(.width(1)) register_4 (.D(MemWrite), .Q(Output), .clk(Clock_Pulse), .clr(Reset));  // open: en
  Register #(.width(1)) register_5 (.D(MemRead), .Q(Output_2), .clk(Clock_Pulse), .clr(Reset));  // open: en
endmodule

module ALU_Control (
  input  [2:0] F,
  output [2:0] ALUOp
);

  wire not_1_out, not_2_out, not_3_out;

  not not_1 (not_1_out, F[1]);
  not not_2 (not_2_out, F[2]);
  not not_3 (not_3_out, F[0]);
  and and_1 (ALUOp[0], not_1_out, F[0]);
  and and_2 (ALUOp[2], F[1], F[0]);

  assign ALUOp[1] = F[1];

  // Notes on the sheet:
  //   Figure: ALU Control Unit
endmodule

module Control_Unit (
  input  [3:0] Instruction_Input,
  output Cin,
  output RegWrite,
  output MemWrite,
  output MemRead,
  output [3:0] ALUOp
);

  wire not_1_out, not_2_out, not_4_out;

  not not_1 (not_1_out, Instruction_Input[3]);
  not not_2 (not_2_out, Instruction_Input[1]);
  not not_3 (MemRead, Instruction_Input[2]);
  not not_4 (not_4_out, Instruction_Input[0]);
  and and_1 (Cin, Instruction_Input[1], Instruction_Input[0]);
  assign ALUOp = {{2{1'b0}}, Instruction_Input[1:0]};  // Bit_Extender bit_extender_1

  assign MemWrite = Instruction_Input[2];
  assign RegWrite = MemRead;
endmodule
